# Fritzing sketch Wemos_DHT22_Levelshifter (saved by Fritzing 0.9.3b)
circuit board: 2.63193cm x 2.14604cm
breadboards: 1

parts:
  J1 = female pin header, 8 pins [form="♀ (female)"]
  J2 = female pin header, 8 pins [form="♀ (female)"]
  BSS138 = MOSFET-NCHANNEL [package=sot23-3]
  R1_10k = Resistor [tolerance=±5% resistance=10k package="1206 [SMD]"]
  C1_100nF = Ceramic Capacitor [capacitance=100nF package="1206 [SMD, multilayer]"]
  R2_10k = Resistor [tolerance=±5% resistance=10k package="1206 [SMD]"]
  DHT22LS_V1_1 = female pin header, 4 pins [form="♀ (female)"]

nets:
  N1: J1.pin6, BSS138.S, R1_10k.Pin_1
  N2: J1.pin7, C1_100nF.1, DHT22LS_V1_1.pin3, DHT22LS_V1_1.pin4
  N3: J1.pin8, C1_100nF.0, R2_10k.Pin_1, DHT22LS_V1_1.pin1
  N4: J2.pin8, BSS138.G, R1_10k.Pin_0
  N5: BSS138.D, R2_10k.Pin_0, DHT22LS_V1_1.pin2

notes:
  RST
  A0
  D0
  D5
  D6
  D7
  D8
  3V3
  TX
  RX
  D1
  D2
  D3
  D4
  GND
  5V
  DHT22
  THIS
  SIDE
  DATA
  VCC
  ------
