# Fritzing sketch Wemos_Honeywell_19C (saved by Fritzing 0.9.3b)
circuit board: 2.68906cm x 4.18926cm
breadboards: 1

parts:
  19C200PA5K = female pin header, 4 pins [form="♀ (female)"]
  J3 = female pin header, 8 pins [form="♀ (female)"]
  J2 = female pin header, 8 pins [form="♀ (female)"]
  C1_10µF = Ceramic Capacitor [capacitance=10µF voltage=16V package="1206 [SMD, multilayer]"]
  LM358 = LM 358 Dual Op-Amp [package="DIP8 [THT]"]
  R1 = Resistor [tolerance=±0.1% resistance=1M package="1206 [SMD]"]
  R2 = Resistor [tolerance=±0.1% resistance=1M package="1206 [SMD]"]
  R3 = Resistor [tolerance=±0.1% resistance=1M package="1206 [SMD]"]
  R4 = Resistor [tolerance=±0.1% resistance=1M package="1206 [SMD]"]
  R5 = Resistor [tolerance=±0.1% resistance=10k package="1206 [SMD]"]
  SCD7805BTG = Voltage Regulator [package=to220-igo]
  R6 = Resistor [tolerance=±5% resistance=100 package="1206 [SMD]"]
  C2_10µF = Ceramic Capacitor [capacitance=10µF voltage=16V package="1206 [SMD, multilayer]"]
  SCD7812BTG1 = Voltage Regulator [package=to220-igo]
  R7 = TRIMPOT [package=3362u-2]
  J5 = Power Jack [package=power_jack_slot]
  D1 = Zener Diode [part_number=1N4732A breakdown_voltage=3.6V package="Melf DO-213 AB [SMD]"]

nets:
  N1: 19C200PA5K.pin1, R1.Pin_0
  N2: 19C200PA5K.pin2, R2.Pin_0
  GND: 19C200PA5K.pin3, J2.pin2, C1_10µF.0, LM358.connector3, R4.Pin_1, SCD7805BTG.GND, R6.Pin_1, C2_10µF.1, SCD7812BTG1.GND, J5.GNDBREAK, J5.GND
  N3: 19C200PA5K.pin4, C1_10µF.1, LM358.connector7, SCD7805BTG.IN, C2_10µF.0, SCD7812BTG1.OUT
  N4: J3.pin2, LM358.connector6, R5.Pin_1, D1.cathode
  N5: J2.pin1, SCD7805BTG.OUT
  N6: LM358.connector0, LM358.connector4, R3.Pin_1
  N7: LM358.connector1, R1.Pin_1, R3.Pin_0
  N8: LM358.connector2, R2.Pin_1, R4.Pin_0
  N9: LM358.connector5, R5.Pin_0, R7.CW
  N10: R6.Pin_0, R7.CCW, R7.WIPER, D1.anode
  N11: SCD7812BTG1.IN, J5.PWR

notes:
  5V
  GND
  D4
  D3
  D2
  D1
  RX
  TX
  3V3
  D8
  D7
  D6
  D5
  D0
  A0
  RST
  IN
  I+
  I-
  O-
  O+
